// Logisim project NitroCompute.circ as structural Verilog: 6 circuits, main circuit main
module main (
);

  wire alu_1_cf_out, alu_1_nf_out, alu_1_zf_out, ALU_OE, ALU_WE, and_1_out, clock_1_out,
       controlled_buffer_1_out, controlled_buffer_2_out, Flag_Registers_cf, Flag_Registers_nf,
       Flag_Registers_zf, gpr_OE, gpr_WE, HALT, IM_OE, IM_WE, IR_OE, IR_WE, MAR_OE, MAR_WE, MBR_Ib_WE,
       MBR_IbE, MBR_OE, MBR_WE, nand_1_out, or_1_out, PC_cEN, PC_LOAD, PC_OE, POWER_OFF_out, POWER_ON_out,
       PWR_in, RA_WE, RAM_OE, RAM_WE, RB_WE, SF;
  wire [2:0] ALU_opc;
  wire [3:0] gpr_Sel;
  wire [7:0] bitselector_2_out, Ex_Address_Bus, Immediate_Value_Register_q, In_Address_Bus,
       Memory_Address_Register_q, Program_Counter_q;
  wire [15:0] alu_1_stored_result, bit_extender_1_out, controlled_buffer_4_out, Ex_Data_Bus, In_Data_Bus,
       Memory_Buffer_Register_q, Random_Access_Memory_dout, Register_A_q, Register_B_q,
       Temporary_Address_Register_q;

  // LedBar #(.inputtype("row"), .matrixcols(16)) ledbar_1: pin names not known
  Button POWER_ON (.out(POWER_ON_out));
  Button POWER_OFF (.out(POWER_OFF_out));
  TheControlUnit thecontrolunit_1 (
    .MBR_Ib_WE(MBR_Ib_WE), .IM_WE(IM_WE), .IM_OE(IM_OE), .ALU_WE(ALU_WE), .ALU_OE(ALU_OE), .PC_LOAD(PC_LOAD),
    .PC_cEN(PC_cEN), .PC_OE(PC_OE), .MAR_WE(MAR_WE), .MAR_OE(MAR_OE), .RAM_WE(RAM_WE), .RAM_OE(RAM_OE),
    .IR_WE(IR_WE), .IR_OE(IR_OE), .RA_WE(RA_WE), .RB_WE(RB_WE), .MBR_WE(MBR_WE), .MBR_OE(MBR_OE),
    .MBR_IbE(MBR_IbE), .SF(SF), .GPR_Sel(gpr_Sel), .ALU_opc(ALU_opc), .GPR_WE(gpr_WE), .GPR_OE(gpr_OE),
    .HALT(HALT), .CF_in(Flag_Registers_cf), .ZF_in(Flag_Registers_zf), .NF_in(Flag_Registers_nf),
    .Power(PWR_in), .Clock_In(controlled_buffer_2_out), .Instruction(Ex_Data_Bus));
  S_R_Flip_Flop s_r_ff_1 (
    .S(POWER_ON_out), .R(1'b0), .clk(clock_1_out), .Q(PWR_in), .reset(controlled_buffer_1_out));  // open: Qn, preset
  assign controlled_buffer_1_out = or_1_out ? 1'b1 : 1'bz;  // Controlled_Buffer controlled_buffer_1
  or or_1 (or_1_out, HALT, POWER_OFF_out);
  Clock clock_1 (.out(clock_1_out));
  assign controlled_buffer_2_out = and_1_out ? clock_1_out : 1'bz;  // Controlled_Buffer controlled_buffer_2
  buf and_1 (and_1_out, PWR_in);  // AND_Gate
  nand nand_1 (nand_1_out, MBR_IbE, gpr_WE);
  Register #(.width(16)) Register_A (
    .D(In_Data_Bus), .en(RA_WE), .clk(controlled_buffer_2_out), .Q(Register_A_q));  // open: clr
  Register #(.width(16)) Register_B (
    .D(In_Data_Bus), .en(RB_WE), .clk(controlled_buffer_2_out), .Q(Register_B_q));  // open: clr
  Counter #(.max('h7f)) Program_Counter (
    .load(PC_LOAD), .up(nand_1_out), .count(PC_cEN), .clk(controlled_buffer_2_out), .D(In_Address_Bus),
    .Q(Program_Counter_q));  // open: clr, carry
  assign In_Address_Bus = PC_OE ? Program_Counter_q : 8'bz;  // Controlled_Buffer controlled_buffer_3
  // LedBar #(.inputtype("row")) ledbar_2: pin names not known; wires that end beside it: In_Address_Bus
  Register #(.width(16)) Temporary_Address_Register (
    .D(In_Data_Bus), .en(IR_WE), .clk(controlled_buffer_2_out), .Q(Temporary_Address_Register_q));  // open: clr
  ALU alu_1 (
    .R1(Register_A_q), .R2(Register_B_q), .WE(ALU_WE), .OE(ALU_OE), .Op_Code(ALU_opc), .D_out(In_Data_Bus),
    .Stored_Result(alu_1_stored_result), .CF_out(alu_1_cf_out), .ZF_out(alu_1_zf_out), .NF_out(alu_1_nf_out));  // open: C_in_1
  BitSelector #(.group(8), .width(16)) bitselector_1 (.in(controlled_buffer_4_out), .out(In_Address_Bus), .sel(1'b0));
  assign controlled_buffer_4_out = IR_OE ? Temporary_Address_Register_q : 16'bz;  // Controlled_Buffer controlled_buffer_4
  BitSelector #(.group(8), .width(16)) bitselector_2 (.in(Ex_Data_Bus), .out(bitselector_2_out), .sel(1'b0));
  // Probe on alu_1_stored_result
  Hex_Digit_Display hex_digit_display_1 (.value(alu_1_stored_result[15:12]));  // open: dp
  Hex_Digit_Display hex_digit_display_2 (.value(alu_1_stored_result[11:8]));  // open: dp
  Register Immediate_Value_Register (
    .D(bitselector_2_out), .en(PC_cEN), .clk(controlled_buffer_2_out), .Q(Immediate_Value_Register_q));  // open: clr
  GeneralPurposeRegisters General_Purpose_Registers (
    .D_out(In_Data_Bus), .WE(gpr_WE), .OE(gpr_OE), .Clock_In(controlled_buffer_2_out), .R_Select(gpr_Sel),
    .D_in(In_Data_Bus));
  Hex_Digit_Display hex_digit_display_3 (.value(alu_1_stored_result[7:4]));  // open: dp
  Hex_Digit_Display hex_digit_display_4 (.value(alu_1_stored_result[3:0]));  // open: dp
  assign bit_extender_1_out = {{8{1'b0}}, Immediate_Value_Register_q};  // Bit_Extender bit_extender_1
  Flags Flag_Registers (
    .CF(Flag_Registers_cf), .ZF(Flag_Registers_zf), .NF(Flag_Registers_nf), .Set_Flags(SF),
    .CF_in(alu_1_cf_out), .ZF_in(alu_1_zf_out), .NF_in(alu_1_nf_out), .Clock_In(controlled_buffer_2_out));
  // LedBar #(.inputtype("row"), .matrixcols(16)) ledbar_3: pin names not known; wires that end beside it: In_Data_Bus
  assign In_Data_Bus = IM_OE ? bit_extender_1_out : 16'bz;  // Controlled_Buffer controlled_buffer_5
  assign Ex_Data_Bus = MBR_Ib_WE ? In_Data_Bus : 16'bz;  // Controlled_Buffer controlled_buffer_6
  assign In_Data_Bus = MBR_IbE ? Memory_Buffer_Register_q : 16'bz;  // Controlled_Buffer controlled_buffer_7
  Register #(.trigger("falling")) Memory_Address_Register (
    .D(In_Address_Bus), .en(MAR_WE), .clk(controlled_buffer_2_out), .Q(Memory_Address_Register_q));  // open: clr
  Register #(.width(16)) Memory_Buffer_Register (
    .D(Ex_Data_Bus), .en(MBR_WE), .clk(controlled_buffer_2_out), .Q(Memory_Buffer_Register_q));  // open: clr
  // LedBar #(.inputtype("row"), .matrixcols(16)) ledbar_4: pin names not known; wires that end beside it: Ex_Data_Bus
  assign Ex_Address_Bus = MAR_OE ? Memory_Address_Register_q : 8'bz;  // Controlled_Buffer controlled_buffer_8
  assign Ex_Data_Bus = MBR_OE ? Memory_Buffer_Register_q : 16'bz;  // Controlled_Buffer controlled_buffer_9
  // LedBar #(.inputtype("row")) ledbar_5: pin names not known; wires that end beside it: Memory_Address_Register_q, Ex_Address_Bus
  // LedBar #(.inputtype("row"), .matrixcols(16)) ledbar_6: pin names not known; wires that end beside it: Ex_Data_Bus
  RAM #(.dataWidth(16), .enables("line")) Random_Access_Memory (
    .addr(Ex_Address_Bus), .we(RAM_WE), .clk(controlled_buffer_2_out), .din(Ex_Data_Bus),
    .dout(Random_Access_Memory_dout));
  assign Ex_Data_Bus = RAM_OE ? Random_Access_Memory_dout : 16'bz;  // Controlled_Buffer controlled_buffer_10

  // Other names for the same wires on the sheet: INSTRUCTION[15:0] = Ex_Data_Bus

  // Notes on the sheet:
  //   0 - ADD
  //   1 - SUB
  //   2 - MULT
  //   3 - DIV
  //   4 - SHL
  //   5 - SHR
  //   6 - AND
  //   7 - OR
  //   NitroCompute ISA (NC- 16)
  //   8 - MOVR
  //   9 - MOVI
  //   A - LOAD
  //   B - STORE
  //   C - JMP
  //   D - JMPZ
  //   E - JMPN
  //   F - NOP/HALT*
  //   Extended ISA (xNC - 16)
  //   ADDC
  //   EXCHANGE
endmodule

module ALU (
  input  [15:0] R1,
  input  [15:0] R2,
  input  C_in_1,
  input  WE,
  input  OE,
  input  [2:0] Op_Code,
  output [15:0] D_out,
  output [15:0] Stored_Result,
  output CF_out,
  output ZF_out,
  output NF_out
);

  wire adder_1_cout, multiplexer_2_out, not_1_out, or_1_out, subtractor_1_bout;
  wire [15:0] adder_1_out, and_1_out, divider_1_out, multiplier_1_out, or_2_out, shifter_1_out,
       shifter_2_out, subtractor_1_out;

  or or_1 (or_1_out, Op_Code[2], Op_Code[1]);
  Adder #(.width(16)) adder_1 (.a(R1), .b(R2), .out(adder_1_out), .cin(C_in_1), .cout(adder_1_cout));
  Subtractor #(.width(16)) subtractor_1 (
    .a(R1), .b(R2), .out(subtractor_1_out), .bin(C_in_1), .bout(subtractor_1_bout));
  Multiplier #(.width(16)) multiplier_1 (.a(R1), .b(R2), .out(multiplier_1_out));  // open: cin, cout
  Divider #(.width(16)) divider_1 (.a(R1), .b(R2), .out(divider_1_out));  // open: upper, rem
  Shifter #(.width(16)) shifter_1 (.in(R1), .\dist (R2[3:0]), .out(shifter_1_out));
  Shifter #(.shift("lr"), .width(16)) shifter_2 (.in(R1), .\dist (R2[3:0]), .out(shifter_2_out));
  assign and_1_out = R1 & R2;  // AND_Gate and_1, 16 bits wide
  assign or_2_out = R1 | R2;  // OR_Gate or_2, 16 bits wide
  not not_1 (not_1_out, or_1_out);
  Multiplexer #(.enable("true"), .select(3), .width(16)) multiplexer_1 (
    .in0(adder_1_out), .in1(subtractor_1_out), .in2(multiplier_1_out), .in3(divider_1_out),
    .in4(shifter_1_out), .in5(shifter_2_out), .in6(and_1_out), .in7(or_2_out), .out(Stored_Result),
    .sel(Op_Code), .en(WE));
  nor nor_1 (ZF_out, Stored_Result[15], Stored_Result[14], Stored_Result[13], Stored_Result[12], Stored_Result[11], Stored_Result[10], Stored_Result[9], Stored_Result[8], Stored_Result[7], Stored_Result[6], Stored_Result[5], Stored_Result[4], Stored_Result[3], Stored_Result[2], Stored_Result[1], Stored_Result[0]);
  Multiplexer multiplexer_2 (.in0(adder_1_cout), .in1(subtractor_1_bout), .out(multiplexer_2_out), .sel(Op_Code[0]));
  and and_2 (CF_out, multiplexer_2_out, not_1_out);
  assign D_out = OE ? Stored_Result : 16'bz;  // Controlled_Buffer controlled_buffer_1
  and and_3 (NF_out, Stored_Result[15], not_1_out);

  // Other names for the same wires on the sheet: tOE = OE; tOPC[2:0] = Op_Code; tWE = WE
endmodule

module RandomTests (
  input  [15:0] in_1,
  input  in_2,
  input  [2:0] in_3,
  input  in_4,
  input  in_5,
  input  in_6,
  input  [3:0] in_7,
  input  in_8,
  input  in_9,
  input  in_10,
  input  in_11,
  input  in_12,
  input  in_13,
  input  in_14,
  input  in_15,
  input  in_16,
  input  in_17,
  input  in_18,
  input  in_19,
  input  in_20,
  input  in_21,
  input  in_22,
  input  in_23,
  input  in_24,
  input  in_25,
  input  in_26,
  input  in_27,
  input  [15:0] in_28,
  input  [15:0] in_29,
  input  in_30,
  input  [15:0] in_31,
  input  [15:0] in_32,
  input  in_33,
  input  [15:0] in_34,
  input  [15:0] in_35,
  input  [15:0] in_36,
  input  in_37
);

  wire clock_1_out, clock_2_out, clock_3_out, controlled_buffer_1_out, controlled_buffer_2_out,
       counter_1_carry, counter_2_carry, counter_2_q, demultiplexer_1_out0, demultiplexer_1_out1,
       demultiplexer_2_out0, demultiplexer_2_out1, demultiplexer_2_out2, demultiplexer_2_out3, not_1_out,
       not_2_out, s_r_ff_1_qn, s_r_ff_2_qn;
  wire [1:0] counter_1_q;
  wire [3:0] binary_to_bcd_converter_1_p2, binary_to_bcd_converter_1_p3;
  wire [15:0] In_Data_Bus, register_1_q, RES, test;

  Clock clock_1 (.out(clock_1_out));
  not not_1 (not_1_out, clock_1_out);
  S_R_Flip_Flop s_r_ff_1 (
    .S(counter_1_carry), .R(1'b0), .clk(not_1_out), .reset(in_30), .Qn(s_r_ff_1_qn));  // open: Q, preset
  S_R_Flip_Flop s_r_ff_2 (
    .S(counter_2_carry), .R(1'b0), .clk(not_2_out), .reset(in_33), .Qn(s_r_ff_2_qn));  // open: Q, preset
  not not_2 (not_2_out, clock_2_out);
  Clock clock_2 (.out(clock_2_out));
  Counter #(.max('h3), .width(2)) counter_1 (
    .clk(controlled_buffer_1_out), .carry(counter_1_carry), .Q(counter_1_q));  // open: clr, load, up, count, D
  assign controlled_buffer_1_out = s_r_ff_1_qn ? clock_1_out : 1'bz;  // Controlled_Buffer controlled_buffer_1
  assign controlled_buffer_2_out = s_r_ff_2_qn ? clock_2_out : 1'bz;  // Controlled_Buffer controlled_buffer_2
  // LedBar #(.inputtype("row"), .matrixcols(16)) ledbar_1: pin names not known; wires that end beside it: RES
  Counter #(.max('h1), .width(1)) counter_2 (
    .clk(controlled_buffer_2_out), .carry(counter_2_carry), .Q(counter_2_q));  // open: clr, load, up, count, D
  // LedBar #(.inputtype("row"), .matrixcols(16)) ledbar_2: pin names not known; wires that end beside it: test
  Demultiplexer demultiplexer_1 (
    .out0(demultiplexer_1_out0), .out1(demultiplexer_1_out1), .in(1'b1), .sel(counter_2_q));
  Demultiplexer #(.select(2)) demultiplexer_2 (
    .out0(demultiplexer_2_out0), .out1(demultiplexer_2_out1), .out2(demultiplexer_2_out2),
    .out3(demultiplexer_2_out3), .in(1'b1), .sel(counter_1_q));
  assign RES = demultiplexer_2_out0 ? in_28 : 16'bz;  // Controlled_Buffer controlled_buffer_3
  assign test = demultiplexer_1_out0 ? in_34 : 16'bz;  // Controlled_Buffer controlled_buffer_4
  assign test = demultiplexer_1_out1 ? in_35 : 16'bz;  // Controlled_Buffer controlled_buffer_5
  assign RES = demultiplexer_2_out1 ? in_32 : 16'bz;  // Controlled_Buffer controlled_buffer_6
  assign RES = demultiplexer_2_out2 ? in_29 : 16'bz;  // Controlled_Buffer controlled_buffer_7
  assign RES = demultiplexer_2_out3 ? in_31 : 16'bz;  // Controlled_Buffer controlled_buffer_8
  // Probe on {13{1'b1}}
  assign In_Data_Bus = in_2 ? in_1 : 16'bz;  // Controlled_Buffer controlled_buffer_9
  // Probe on nothing
  Clock clock_3 (.out(clock_3_out));
  Register #(.width(16)) register_1 (.D(in_36), .en(in_37), .clk(clock_3_out), .Q(register_1_q));  // open: clr
  // Binary_to_BCD_converter #(.binvalue(13)) binary_to_bcd_converter_1: pin names not known; wires that end beside it: {13{1'b1}}, binary_to_bcd_converter_1_p2, binary_to_bcd_converter_1_p3
  Adder #(.width(4)) adder_1 (
    .a(binary_to_bcd_converter_1_p2), .b(binary_to_bcd_converter_1_p3));  // open: out, cin, cout
  // Probe on register_1_q

  // Other names for the same wires on the sheet: ALU_OE = in_16; ALU_opc[2:0] = in_3; ALU_WE = in_10; gpr_OE = in_20;
  //   gpr_Sel[3:0] = in_7; gpr_WE = in_14; IM_OE = in_27; IM_WE = in_21; IR_OE = in_12; IR_WE = in_5; MAR_OE = in_11;
  //   MAR_WE = in_4; MBR_Ib_WE = in_9; MBR_IbE = in_19; MBR_OE = in_13; MBR_WE = in_6; PC_cEN = in_15; PC_LOAD = in_8;
  //   PC_OE = in_22; RA_WE = in_18; RAM_OE = in_23; RAM_WE = in_17; RB_WE = in_24; SF = in_25;
  //   Test_Ex_Ad_B_En = in_26

  // Notes on the sheet:
  //   Two step counter for MOVR
  //   Debug inputs for main
  //   Circuit which gives a One only at beginning and then the rest is based on another input
endmodule

module GeneralPurposeRegisters (
  input  [15:0] D_in,
  input  [3:0] R_Select,
  input  WE,
  input  OE,
  input  Clock_In,
  output [15:0] D_out
);

  wire demultiplexer_1_out0, demultiplexer_1_out1, demultiplexer_1_out2, demultiplexer_1_out3,
       demultiplexer_1_out4, demultiplexer_1_out5, demultiplexer_1_out6, demultiplexer_1_out7,
       demultiplexer_1_out8, demultiplexer_1_out9, demultiplexer_1_out10, demultiplexer_1_out11,
       demultiplexer_1_out12, demultiplexer_1_out13, demultiplexer_1_out14, demultiplexer_1_out15;
  wire [15:0] multiplexer_1_out, r0_out, r1_out, r2_out, r3_out, r4_out, r5_out, r6_out, r7_out, r8_out,
       r9_out, r10_out, r11_out, r12_out, r13_out, r14_out, r15_out;

  Register #(.width(16)) R0 (.D(D_in), .en(demultiplexer_1_out0), .clk(Clock_In), .Q(r0_out));  // open: clr
  Register #(.width(16)) R1 (.D(D_in), .en(demultiplexer_1_out1), .clk(Clock_In), .Q(r1_out));  // open: clr
  Register #(.width(16)) R2 (.D(D_in), .en(demultiplexer_1_out2), .clk(Clock_In), .Q(r2_out));  // open: clr
  Register #(.width(16)) R3 (.D(D_in), .en(demultiplexer_1_out3), .clk(Clock_In), .Q(r3_out));  // open: clr
  Register #(.width(16)) R4 (.D(D_in), .en(demultiplexer_1_out4), .clk(Clock_In), .Q(r4_out));  // open: clr
  Register #(.width(16)) R5 (.D(D_in), .en(demultiplexer_1_out5), .clk(Clock_In), .Q(r5_out));  // open: clr
  Register #(.width(16)) R6 (.D(D_in), .en(demultiplexer_1_out6), .clk(Clock_In), .Q(r6_out));  // open: clr
  Register #(.width(16)) R7 (.D(D_in), .en(demultiplexer_1_out7), .clk(Clock_In), .Q(r7_out));  // open: clr
  Demultiplexer #(.enable("true"), .select(4)) demultiplexer_1 (
    .out0(demultiplexer_1_out0), .out1(demultiplexer_1_out1), .out2(demultiplexer_1_out2),
    .out3(demultiplexer_1_out3), .out4(demultiplexer_1_out4), .out5(demultiplexer_1_out5),
    .out6(demultiplexer_1_out6), .out7(demultiplexer_1_out7), .out8(demultiplexer_1_out8),
    .out9(demultiplexer_1_out9), .out10(demultiplexer_1_out10), .out11(demultiplexer_1_out11),
    .out12(demultiplexer_1_out12), .out13(demultiplexer_1_out13), .out14(demultiplexer_1_out14),
    .out15(demultiplexer_1_out15), .in(1'b1), .sel(R_Select), .en(WE));
  Register #(.width(16)) R8 (.D(D_in), .en(demultiplexer_1_out8), .clk(Clock_In), .Q(r8_out));  // open: clr
  Register #(.width(16)) R9 (.D(D_in), .en(demultiplexer_1_out9), .clk(Clock_In), .Q(r9_out));  // open: clr
  Register #(.width(16)) R10 (.D(D_in), .en(demultiplexer_1_out10), .clk(Clock_In), .Q(r10_out));  // open: clr
  Register #(.width(16)) R11 (.D(D_in), .en(demultiplexer_1_out11), .clk(Clock_In), .Q(r11_out));  // open: clr
  Register #(.width(16)) R12 (.D(D_in), .en(demultiplexer_1_out12), .clk(Clock_In), .Q(r12_out));  // open: clr
  Register #(.width(16)) R13 (.D(D_in), .en(demultiplexer_1_out13), .clk(Clock_In), .Q(r13_out));  // open: clr
  Register #(.width(16)) R14 (.D(D_in), .en(demultiplexer_1_out14), .clk(Clock_In), .Q(r14_out));  // open: clr
  Register #(.width(16)) R15 (.D(D_in), .en(demultiplexer_1_out15), .clk(Clock_In), .Q(r15_out));  // open: clr
  Multiplexer #(.select(4), .width(16)) multiplexer_1 (
    .in0(r0_out), .in1(r1_out), .in2(r2_out), .in3(r3_out), .in4(r4_out), .in5(r5_out), .in6(r6_out),
    .in7(r7_out), .in8(r8_out), .in9(r9_out), .in10(r10_out), .in11(r11_out), .in12(r12_out), .in13(r13_out),
    .in14(r14_out), .in15(r15_out), .out(multiplexer_1_out), .sel(R_Select));
  assign D_out = OE ? multiplexer_1_out : 16'bz;  // Controlled_Buffer controlled_buffer_1

  // Other names for the same wires on the sheet: rb_OE = OE; rb_Sel[3:0] = R_Select
endmodule

module TheControlUnit (
  input  Power,
  input  [15:0] Instruction,
  input  CF_in,
  input  ZF_in,
  input  NF_in,
  input  Clock_In,
  output [2:0] ALU_opc,
  output MBR_Ib_WE,
  output IM_WE,
  output IM_OE,
  output ALU_WE,
  output ALU_OE,
  output PC_LOAD,
  output PC_cEN,
  output PC_OE,
  output MAR_WE,
  output MAR_OE,
  output RAM_WE,
  output RAM_OE,
  output IR_WE,
  output IR_OE,
  output RA_WE,
  output RB_WE,
  output MBR_WE,
  output MBR_OE,
  output MBR_IbE,
  output SF,
  output [3:0] GPR_Sel,
  output GPR_WE,
  output GPR_OE,
  output HALT
);

  wire ADD, ALU, ALU_Counter_q, ALU_Counter_qn, and_1_out, and_2_out, and_3_out, and_4_out, and_5_out,
       and_6_out, and_7_out, and_9_out, and_10_out, and_11_out, and_12_out, and_13_out, and_14_out, AND_ALU,
       controlled_buffer_1_out, controlled_buffer_2_out, controlled_buffer_4_out, controlled_buffer_11_out,
       controlled_buffer_18_out, controlled_buffer_20_out, controlled_buffer_30_out,
       controlled_buffer_33_out, controlled_buffer_47_out, counter_1_carry, counter_2_carry, counter_3_carry,
       counter_4_carry, counter_5_carry, counter_6_carry, counter_7_carry, counter_8_carry,
       demultiplexer_2_out0, demultiplexer_2_out1, demultiplexer_2_out2, demultiplexer_3_out0,
       demultiplexer_3_out1, demultiplexer_3_out2, demultiplexer_4_out0, demultiplexer_4_out1,
       demultiplexer_4_out2, demultiplexer_5_out0, demultiplexer_5_out1, demultiplexer_5_out2,
       demultiplexer_6_out0, demultiplexer_6_out1, demultiplexer_6_out2, demultiplexer_6_out3,
       demultiplexer_7_out0, demultiplexer_7_out1, demultiplexer_7_out2, demultiplexer_7_out3,
       demultiplexer_7_out4, demultiplexer_8_out0, demultiplexer_8_out1, demultiplexer_8_out2,
       demultiplexer_8_out3, demultiplexer_8_out4, demultiplexer_8_out5, demultiplexer_9_out0,
       demultiplexer_9_out1, demultiplexer_9_out2, demultiplexer_9_out3, DIV, FETCH, GET_NEXT, IS_OP, JMP,
       JMPN, JMPZ, ledbar_1_p2, ledbar_3_p2, LOAD, LOAD_Counter_q, LOAD_Counter_qn, MOVI, MOVI_Counter_q,
       MOVI_Counter_qn, MOVR, MOVR_Counter_q, MOVR_Counter_qn, MULT, nor_1_out, not_1_out, not_2_out,
       not_3_out, not_4_out, not_6_out, not_7_out, not_8_out, not_9_out, or_1_out, or_2_out, or_3_out,
       or_5_out, or_6_out, or_7_out, or_8_out, or_9_out, or_10_out, OR_ALU, PWR_in, RESET_COUNTER, RSTORE,
       s_r_ff_1_q, s_r_ff_1_qn, s_r_ff_2_q, s_r_ff_2_qn, s_r_ff_4_q, s_r_ff_4_qn, SHL, SHR, STORE,
       STORE_Counter_q, STORE_Counter_qn, SUB;
  wire [1:0] counter_1_q, counter_2_q, counter_3_q, counter_4_q, counter_5_q, counter_8_q;
  wire [2:0] ALU_opc_t, counter_6_q, counter_7_q;
  wire [3:0] RS1;
  wire [3:3] op_code;
  wire [7:0] IMM;
  wire [15:0] controlled_buffer_3_out;
  wire [28:0] ALU1, ALU2, ALU3, JMP1, JMPN1, JMPZ1, LOAD1, LOAD2, MOVI1, MOVI2, MOVR1, MOVR2, SELECT_LINES,
       STORE1, STORE2, STORE3;

  Demultiplexer #(.select(4)) demultiplexer_1 (
    .out0(ADD), .out1(SUB), .out2(MULT), .out3(DIV), .out4(SHL), .out5(SHR), .out6(AND_ALU), .out7(OR_ALU),
    .out8(MOVR), .out9(MOVI), .out10(LOAD), .out11(STORE), .out12(JMP), .out13(JMPZ), .out14(JMPN),
    .out15(FETCH), .in(1'b1), .sel({op_code[3], ALU_opc_t}));
  S_R_Flip_Flop s_r_ff_1 (
    .S(counter_1_carry), .R(1'b0), .clk(not_1_out), .Q(s_r_ff_1_q), .reset(RESET_COUNTER), .Qn(s_r_ff_1_qn));  // open: preset
  not not_1 (not_1_out, and_1_out);
  // LedBar #(.inputtype("row"), .matrixcols(29)) ledbar_1: pin names not known; wires that end beside it: SELECT_LINES, ledbar_1_p2, ledbar_1_p2
  S_R_Flip_Flop s_r_ff_2 (
    .S(counter_2_carry), .R(1'b0), .clk(not_2_out), .Q(s_r_ff_2_q), .reset(RESET_COUNTER), .Qn(s_r_ff_2_qn));  // open: preset
  not not_2 (not_2_out, and_1_out);
  S_R_Flip_Flop s_r_ff_3 (.S(Power), .R(1'b0), .clk(Clock_In), .Q(PWR_in), .reset(HALT));  // open: Qn, preset
  or or_1 (or_1_out, FETCH, GET_NEXT);
  and and_1 (and_1_out, ~1'b0, Clock_In);  // AND_Gate
  not not_3 (not_3_out, and_1_out);
  Counter #(.max('h2), .width(2)) counter_1 (
    .clr(RESET_COUNTER), .clk(controlled_buffer_1_out), .carry(counter_1_carry), .Q(counter_1_q));  // open: load, up, count, D
  assign controlled_buffer_1_out = s_r_ff_1_qn ? and_1_out : 1'bz;  // Controlled_Buffer controlled_buffer_1
  Counter #(.max('h2), .width(2)) counter_2 (
    .clr(RESET_COUNTER), .clk(controlled_buffer_2_out), .carry(counter_2_carry), .Q(counter_2_q));  // open: load, up, count, D
  assign controlled_buffer_2_out = s_r_ff_2_qn ? and_1_out : 1'bz;  // Controlled_Buffer controlled_buffer_2
  assign controlled_buffer_3_out = PWR_in ? Instruction : 16'bz;  // Controlled_Buffer controlled_buffer_3
  S_R_Flip_Flop MOVR_Counter (
    .S(counter_3_carry), .R(1'b0), .clk(not_3_out), .Q(MOVR_Counter_q), .reset(RESET_COUNTER),
    .Qn(MOVR_Counter_qn));  // open: preset
  // LedBar #(.inputtype("row"), .matrixcols(29)) ledbar_2: pin names not known; wires that end beside it: SELECT_LINES
  and and_2 (and_2_out, s_r_ff_1_q, JMP);
  and and_3 (and_3_out, s_r_ff_2_q, JMPN);
  Register #(.width(16)) Internal_Instruction_Register (
    .D(controlled_buffer_3_out), .en(or_1_out), .clk(Clock_In), .Q({op_code[3], ALU_opc_t, RS1, IMM}));  // open: clr
  and and_4 (and_4_out, MOVR_Counter_q, MOVR);
  Counter #(.max('h2), .width(2)) counter_3 (
    .clr(RESET_COUNTER), .clk(controlled_buffer_4_out), .carry(counter_3_carry), .Q(counter_3_q));  // open: load, up, count, D
  assign controlled_buffer_4_out = MOVR_Counter_qn ? and_1_out : 1'bz;  // Controlled_Buffer controlled_buffer_4
  assign MOVR1 = MOVR ? {2'b10, IMM[7:4], 23'h80008} : 29'bz;  // Controlled_Buffer controlled_buffer_5
  Demultiplexer #(.enable("true"), .select(2)) demultiplexer_2 (
    .out0(demultiplexer_2_out0), .out1(demultiplexer_2_out1), .out2(demultiplexer_2_out2), .in(1'b1),
    .sel(counter_1_q), .en(JMP));  // open: out3
  assign JMP1 = JMP ? 29'h18120 : 29'bz;  // Controlled_Buffer controlled_buffer_6
  Demultiplexer #(.enable("true"), .select(2)) demultiplexer_3 (
    .out0(demultiplexer_3_out0), .out1(demultiplexer_3_out1), .out2(demultiplexer_3_out2), .in(1'b1),
    .sel(counter_2_q), .en(JMPN));  // open: out3
  assign SELECT_LINES = demultiplexer_2_out2 ? 29'h5e00 : 29'bz;  // Controlled_Buffer controlled_buffer_7
  assign SELECT_LINES = or_2_out ? JMP1 : 29'bz;  // Controlled_Buffer controlled_buffer_8
  or or_2 (or_2_out, demultiplexer_2_out0, demultiplexer_2_out1);
  assign SELECT_LINES = demultiplexer_3_out2 ? 29'h5e00 : 29'bz;  // Controlled_Buffer controlled_buffer_9
  assign SELECT_LINES = or_3_out ? JMPN1 : 29'bz;  // Controlled_Buffer controlled_buffer_10
  or or_3 (or_3_out, demultiplexer_3_out0, demultiplexer_3_out1);
  Multiplexer #(.width(29)) multiplexer_1 (.in0({29{1'b0}}), .in1(29'h18100), .out(JMPN1), .sel(and_5_out));
  and and_5 (and_5_out, JMPN, NF_in);
  assign controlled_buffer_11_out = MOVR ? and_4_out : 1'bz;  // Controlled_Buffer controlled_buffer_11
  Demultiplexer #(.enable("true"), .select(2)) demultiplexer_4 (
    .out0(demultiplexer_4_out0), .out1(demultiplexer_4_out1), .out2(demultiplexer_4_out2), .in(1'b1),
    .sel(counter_3_q), .en(MOVR));  // open: out3
  assign SELECT_LINES = demultiplexer_4_out2 ? 29'h5e00 : 29'bz;  // Controlled_Buffer controlled_buffer_12
  assign SELECT_LINES = demultiplexer_4_out0 ? MOVR1 : 29'bz;  // Controlled_Buffer controlled_buffer_13
  assign SELECT_LINES = demultiplexer_4_out1 ? MOVR2 : 29'bz;  // Controlled_Buffer controlled_buffer_14
  assign MOVR2 = MOVR ? {2'b01, RS1, 23'h300000} : 29'bz;  // Controlled_Buffer controlled_buffer_15
  not not_4 (not_4_out, and_1_out);
  or or_4 (IS_OP, SUB, MULT, DIV, SHL, SHR, AND_ALU, OR_ALU, ADD, MOVR, MOVI, LOAD, STORE, JMP, JMPZ, JMPN);
  S_R_Flip_Flop s_r_ff_4 (
    .S(counter_4_carry), .R(1'b0), .clk(not_4_out), .Q(s_r_ff_4_q), .reset(RESET_COUNTER), .Qn(s_r_ff_4_qn));  // open: preset
  not not_5 (ALU, op_code[3]);
  assign RESET_COUNTER = Clock_In ? GET_NEXT : 1'bz;  // Controlled_Buffer controlled_buffer_16
  assign controlled_buffer_11_out = JMP ? and_2_out : 1'bz;  // Controlled_Buffer controlled_buffer_17
  and and_6 (and_6_out, s_r_ff_4_q, JMPZ);
  Counter #(.max('h2), .width(2)) counter_4 (
    .clr(RESET_COUNTER), .clk(controlled_buffer_18_out), .carry(counter_4_carry), .Q(counter_4_q));  // open: load, up, count, D
  assign controlled_buffer_18_out = s_r_ff_4_qn ? and_1_out : 1'bz;  // Controlled_Buffer controlled_buffer_18
  and and_7 (and_7_out, JMPZ, ZF_in);
  and and_8 (HALT, op_code[3], ALU_opc_t[0], ALU_opc_t[1], ALU_opc_t[2], RS1[0], RS1[1], RS1[2], RS1[3], IMM[7], IMM[6], IMM[5], IMM[4], IMM[3], IMM[2], IMM[1], IMM[0]);
  not not_6 (not_6_out, and_1_out);
  Multiplexer #(.width(29)) multiplexer_2 (.in0({29{1'b0}}), .in1(29'h18100), .out(JMPZ1), .sel(and_7_out));
  assign controlled_buffer_11_out = JMPZ ? and_6_out : 1'bz;  // Controlled_Buffer controlled_buffer_19
  S_R_Flip_Flop MOVI_Counter (
    .S(counter_5_carry), .R(1'b0), .clk(not_6_out), .Q(MOVI_Counter_q), .reset(RESET_COUNTER),
    .Qn(MOVI_Counter_qn));  // open: preset
  // LedBar #(.inputtype("row"), .matrixcols(29)) ledbar_3: pin names not known; wires that end beside it: SELECT_LINES, ledbar_3_p2, ledbar_3_p2
  Demultiplexer #(.enable("true"), .select(2)) demultiplexer_5 (
    .out0(demultiplexer_5_out0), .out1(demultiplexer_5_out1), .out2(demultiplexer_5_out2), .in(1'b1),
    .sel(counter_4_q), .en(JMPZ));  // open: out3
  and and_9 (and_9_out, MOVI_Counter_q, MOVI);
  Counter #(.max('h3), .width(2)) counter_5 (
    .clr(RESET_COUNTER), .clk(controlled_buffer_20_out), .carry(counter_5_carry), .Q(counter_5_q));  // open: load, up, count, D
  assign controlled_buffer_20_out = MOVI_Counter_qn ? and_1_out : 1'bz;  // Controlled_Buffer controlled_buffer_20
  assign MOVI1 = MOVI ? 29'h10 : 29'bz;  // Controlled_Buffer controlled_buffer_21
  assign SELECT_LINES = or_5_out ? JMPZ1 : 29'bz;  // Controlled_Buffer controlled_buffer_22
  or or_5 (or_5_out, demultiplexer_5_out0, demultiplexer_5_out1);
  nor nor_1 (nor_1_out, FETCH, GET_NEXT);
  assign controlled_buffer_11_out = JMPN ? and_3_out : 1'bz;  // Controlled_Buffer controlled_buffer_23
  assign SELECT_LINES = demultiplexer_5_out2 ? 29'h5e00 : 29'bz;  // Controlled_Buffer controlled_buffer_24
  Multiplexer #(.width(29)) multiplexer_3 (
    .in0(29'h5e00), .in1(SELECT_LINES),
    .out({GPR_OE, GPR_WE, GPR_Sel, SF, MBR_IbE, MBR_OE, MBR_WE, RB_WE, RA_WE, IR_OE, IR_WE, RAM_OE, RAM_WE, MAR_OE, MAR_WE, PC_OE, PC_cEN, PC_LOAD, ALU_OE, ALU_WE, IM_OE, IM_WE, MBR_Ib_WE, ALU_opc}),
    .sel(nor_1_out));
  assign controlled_buffer_11_out = MOVI ? and_9_out : 1'bz;  // Controlled_Buffer controlled_buffer_25
  Demultiplexer #(.enable("true"), .select(2)) demultiplexer_6 (
    .out0(demultiplexer_6_out0), .out1(demultiplexer_6_out1), .out2(demultiplexer_6_out2),
    .out3(demultiplexer_6_out3), .in(1'b1), .sel(counter_5_q), .en(MOVI));
  assign SELECT_LINES = or_6_out ? MOVI1 : 29'bz;  // Controlled_Buffer controlled_buffer_26
  or or_6 (or_6_out, demultiplexer_6_out0, demultiplexer_6_out1);
  assign SELECT_LINES = demultiplexer_6_out2 ? MOVI2 : 29'bz;  // Controlled_Buffer controlled_buffer_27
  Multiplexer multiplexer_4 (.in0(1'b0), .in1(controlled_buffer_11_out), .out(GET_NEXT), .sel(IS_OP));
  assign SELECT_LINES = demultiplexer_6_out3 ? 29'h5e00 : 29'bz;  // Controlled_Buffer controlled_buffer_28
  assign MOVI2 = MOVI ? {2'b01, RS1, 23'h20} : 29'bz;  // Controlled_Buffer controlled_buffer_29
  not not_7 (not_7_out, and_1_out);
  S_R_Flip_Flop LOAD_Counter (
    .S(counter_7_carry), .R(1'b0), .clk(not_8_out), .Q(LOAD_Counter_q), .reset(RESET_COUNTER),
    .Qn(LOAD_Counter_qn));  // open: preset
  not not_8 (not_8_out, and_1_out);
  // LedBar #(.inputtype("row"), .matrixcols(29)) ledbar_4: pin names not known; wires that end beside it: SELECT_LINES, 1'b0
  S_R_Flip_Flop ALU_Counter (
    .S(counter_6_carry), .R(1'b0), .clk(not_7_out), .Q(ALU_Counter_q), .reset(RESET_COUNTER),
    .Qn(ALU_Counter_qn));  // open: preset
  // LedBar #(.inputtype("row"), .matrixcols(29)) ledbar_5: pin names not known; wires that end beside it: ALU_opc_t[1], SELECT_LINES
  and and_10 (and_10_out, ALU_Counter_q, ALU);
  Counter #(.max('h4), .width(3)) counter_6 (
    .clr(RESET_COUNTER), .clk(controlled_buffer_30_out), .carry(counter_6_carry), .Q(counter_6_q));  // open: load, up, count, D
  assign controlled_buffer_30_out = ALU_Counter_qn ? and_1_out : 1'bz;  // Controlled_Buffer controlled_buffer_30
  assign ALU1 = ALU ? {2'b10, RS1, 20'h4000, ALU_opc_t} : 29'bz;  // Controlled_Buffer controlled_buffer_31
  assign controlled_buffer_11_out = LOAD ? and_11_out : 1'bz;  // Controlled_Buffer controlled_buffer_32
  and and_11 (and_11_out, LOAD_Counter_q, LOAD);
  Counter #(.max('h4), .width(3)) counter_7 (
    .clr(RESET_COUNTER), .clk(controlled_buffer_33_out), .carry(counter_7_carry), .Q(counter_7_q));  // open: load, up, count, D
  assign controlled_buffer_33_out = LOAD_Counter_qn ? and_1_out : 1'bz;  // Controlled_Buffer controlled_buffer_33
  assign LOAD1 = LOAD ? 29'h9d820 : 29'bz;  // Controlled_Buffer controlled_buffer_34
  Demultiplexer #(.enable("true"), .select(3)) demultiplexer_7 (
    .out0(demultiplexer_7_out0), .out1(demultiplexer_7_out1), .out2(demultiplexer_7_out2),
    .out3(demultiplexer_7_out3), .out4(demultiplexer_7_out4), .in(1'b1), .sel(counter_7_q), .en(LOAD));  // open: out5, out6, out7
  Demultiplexer #(.enable("true"), .select(3)) demultiplexer_8 (
    .out0(demultiplexer_8_out0), .out1(demultiplexer_8_out1), .out2(demultiplexer_8_out2),
    .out3(demultiplexer_8_out3), .out4(demultiplexer_8_out4), .out5(demultiplexer_8_out5), .in(1'b1),
    .sel(counter_6_q), .en(ALU));  // open: out6, out7
  or or_7 (or_7_out, demultiplexer_8_out5, demultiplexer_8_out4);
  assign ALU2 = ALU ? {2'b10, IMM[7:4], 20'h8001, ALU_opc_t} : 29'bz;  // Controlled_Buffer controlled_buffer_35
  assign controlled_buffer_11_out = ALU ? and_10_out : 1'bz;  // Controlled_Buffer controlled_buffer_36
  assign SELECT_LINES = or_8_out ? LOAD1 : 29'bz;  // Controlled_Buffer controlled_buffer_37
  or or_8 (or_8_out, demultiplexer_7_out0, demultiplexer_7_out1);
  or or_9 (or_9_out, demultiplexer_7_out3, demultiplexer_7_out4);
  assign SELECT_LINES = demultiplexer_7_out2 ? LOAD2 : 29'bz;  // Controlled_Buffer controlled_buffer_38
  assign SELECT_LINES = or_10_out ? ALU1 : 29'bz;  // Controlled_Buffer controlled_buffer_39
  or or_10 (or_10_out, demultiplexer_8_out0, demultiplexer_8_out1);
  assign SELECT_LINES = or_9_out ? 29'h5e00 : 29'bz;  // Controlled_Buffer controlled_buffer_40
  assign LOAD2 = LOAD ? {2'b01, RS1, 23'h200200} : 29'bz;  // Controlled_Buffer controlled_buffer_41
  assign SELECT_LINES = demultiplexer_8_out2 ? ALU2 : 29'bz;  // Controlled_Buffer controlled_buffer_42
  assign SELECT_LINES = demultiplexer_8_out3 ? ALU3 : 29'bz;  // Controlled_Buffer controlled_buffer_43
  assign SELECT_LINES = or_7_out ? 29'h5e00 : 29'bz;  // Controlled_Buffer controlled_buffer_44
  assign controlled_buffer_11_out = STORE ? and_13_out : 1'bz;  // Controlled_Buffer controlled_buffer_45
  assign ALU3 = ALU ? {2'b01, IMM[3:0], 20'h80018, ALU_opc_t} : 29'bz;  // Controlled_Buffer controlled_buffer_46
  S_R_Flip_Flop STORE_Counter (
    .S(counter_8_carry), .R(1'b0), .clk(not_9_out), .Q(STORE_Counter_q), .reset(RESET_COUNTER),
    .Qn(STORE_Counter_qn));  // open: preset
  not not_9 (not_9_out, and_1_out);
  Counter #(.max('h3), .width(2)) counter_8 (
    .clr(RESET_COUNTER), .clk(controlled_buffer_47_out), .carry(counter_8_carry), .Q(counter_8_q));  // open: load, up, count, D
  assign controlled_buffer_47_out = STORE_Counter_qn ? and_1_out : 1'bz;  // Controlled_Buffer controlled_buffer_47
  // LedBar #(.inputtype("row"), .matrixcols(29)) ledbar_6: pin names not known; wires that end beside it: 1'b0, 1'b0, SELECT_LINES
  assign STORE1 = and_12_out ? 29'h18820 : 29'bz;  // Controlled_Buffer controlled_buffer_48
  and and_12 (and_12_out, STORE, ~RSTORE);  // AND_Gate
  and and_13 (and_13_out, STORE_Counter_q, STORE);
  Demultiplexer #(.enable("true"), .select(2)) demultiplexer_9 (
    .out0(demultiplexer_9_out0), .out1(demultiplexer_9_out1), .out2(demultiplexer_9_out2),
    .out3(demultiplexer_9_out3), .in(1'b1), .sel(counter_8_q), .en(STORE));
  assign STORE2 = STORE ? {2'b10, RS1, 23'h90808} : 29'bz;  // Controlled_Buffer controlled_buffer_49
  nor nor_2 (RSTORE, IMM[4], IMM[5], IMM[6], IMM[7]);
  assign SELECT_LINES = demultiplexer_9_out3 ? 29'h5e00 : 29'bz;  // Controlled_Buffer controlled_buffer_50
  assign SELECT_LINES = demultiplexer_9_out0 ? STORE1 : 29'bz;  // Controlled_Buffer controlled_buffer_51
  assign SELECT_LINES = demultiplexer_9_out1 ? STORE2 : 29'bz;  // Controlled_Buffer controlled_buffer_52
  assign SELECT_LINES = demultiplexer_9_out2 ? STORE3 : 29'bz;  // Controlled_Buffer controlled_buffer_53
  assign STORE3 = STORE ? 29'h103000 : 29'bz;  // Controlled_Buffer controlled_buffer_54
  assign STORE1 = and_14_out ? {2'b10, IMM[3:0], 23'h18800} : 29'bz;  // Controlled_Buffer controlled_buffer_55
  and and_14 (and_14_out, STORE, RSTORE);

  // Other names for the same wires on the sheet: RS2[3:0] = IMM[7:4]; op_code[2:0] = ALU_opc_t;
  //   RT[3:0] = {IMM[0], IMM[1], IMM[2], IMM[3]}; CF = CF_in; CLK = Clock_In; NF = NF_in; ZF = ZF_in

  // Notes on the sheet:
  //   JMP
  //   JMPN
  //   Two step counter for MOVR
  //   JMPZ
  //   Two step counter for MOVI
  //   Two step counter for LOAD
  //   Three step counter for ALU operations
  //   Three step counter for STORE
  //   RSTORE gets address from register RT, using RS2 to determine STORE type
endmodule

module Flags (
  input  Set_Flags,
  input  CF_in,
  input  ZF_in,
  input  NF_in,
  input  Clock_In,
  output CF,
  output ZF,
  output NF
);

  Register #(.width(1)) Carry_Flag (.D(CF_in), .en(Set_Flags), .clk(Clock_In), .Q(CF));  // open: clr
  Register #(.width(1)) Zero_Flag (.D(ZF_in), .en(Set_Flags), .clk(Clock_In), .Q(ZF));  // open: clr
  Register #(.width(1)) Negative_Flag (.D(NF_in), .en(Set_Flags), .clk(Clock_In), .Q(NF));  // open: clr
endmodule
